// Logisim project alu.circ as structural Verilog: 1 circuit, main circuit alu
module alu (
  input  [31:0] A,
  input  [31:0] B,
  input  [3:0] ALUSel,
  output [31:0] Result
);

  wire adder_2_cout, comparator_1_lt;
  wire [31:0] ADD0, adder_3_out, adder_6_out, AND0, ASIGN, BSEL0, BSIGN, DIVU0, MUL0, MULH0, MULHU0,
       multiplexer_5_out, multiplier_2_cout, multiplier_3_cout, multiplier_3_out, multiplier_4_cout,
       multiplier_4_out, multiplier_5_cout, multiplier_5_out, negator_1_out, negator_2_out, negator_3_out,
       OR0, REMU0, SLL0, SLT0, SRA0, SRL0, SUB0, subtractor_2_out, TEMP, XOR0;

  // Probe on ADD0
  Adder #(.width(32)) adder_1 (.a(A), .b(B), .out(ADD0));  // open: cin, cout
  assign AND0 = A & B;  // AND_Gate AND0, 32 bits wide
  assign OR0 = A | B;  // OR_Gate OR0, 32 bits wide
  assign XOR0 = A ^ B;  // XOR_Gate XOR0, 32 bits wide
  Shifter #(.width(32), .shift("lr")) shifter_1 (.in(A), .\dist (B[4:0]), .out(SRL0));
  Shifter #(.width(32), .shift("ar")) shifter_2 (.in(A), .\dist (B[4:0]), .out(SRA0));
  Shifter #(.width(32)) shifter_3 (.in(A), .\dist (B[4:0]), .out(SLL0));
  Comparator #(.width(32)) comparator_1 (.a(A), .b(B), .lt(comparator_1_lt));  // open: gt, eq
  Divider #(.width(32)) divider_1 (.a(A), .b(B), .out(DIVU0), .rem(REMU0));  // open: upper
  // Probe on MUL0
  Multiplier #(.width(32)) multiplier_1 (.a(A), .b(B), .out(MUL0), .cout(MULHU0));  // open: cin
  // Probe on MULHU0
  Subtractor #(.width(32)) subtractor_1 (.a(A), .b(B), .out(SUB0));  // open: bin, bout
  Multiplexer #(.width(32), .enable("false")) multiplexer_1 (.in0(A), .in1(B), .out(BSEL0), .sel(1'b1));
  Multiplexer #(.width(32), .enable("false")) multiplexer_2 (
    .in0({32{1'b0}}), .in1(32'h80000000), .out(ASIGN), .sel(A[31]));
  Multiplexer #(.width(32), .enable("false")) multiplexer_3 (
    .in0({32{1'b0}}), .in1(32'h80000000), .out(BSIGN), .sel(B[31]));
  assign SLT0 = {{31{1'b0}}, comparator_1_lt};  // Bit_Extender bit_extender_1
  Multiplier #(.width(32)) multiplier_2 (.a(ASIGN), .b(BSIGN), .cout(multiplier_2_cout));  // open: out, cin
  Multiplier #(.width(32)) multiplier_3 (
    .a({1'b0, A[30:0]}), .b({1'b0, B[30:0]}), .out(multiplier_3_out), .cout(multiplier_3_cout));  // open: cin
  Multiplier #(.width(32)) multiplier_4 (
    .a(ASIGN), .b({1'b0, B[30:0]}), .out(multiplier_4_out), .cout(multiplier_4_cout));  // open: cin
  Multiplier #(.width(32)) multiplier_5 (
    .a({1'b0, A[30:0]}), .b(BSIGN), .out(multiplier_5_out), .cout(multiplier_5_cout));  // open: cin
  Adder #(.width(32)) adder_2 (.a(multiplier_3_out), .b(TEMP), .cout(adder_2_cout));  // open: out, cin
  Adder #(.width(32)) adder_3 (.a(multiplier_2_cout), .b(multiplier_3_cout), .out(adder_3_out));  // open: cin, cout
  Adder #(.width(32)) adder_4 (.a(adder_3_out), .b(multiplexer_5_out), .out(MULH0), .cin(adder_2_cout));  // open: cout
  Negator #(.width(32)) negator_1 (.in(multiplier_4_out), .out(negator_1_out));
  Adder #(.width(32)) adder_5 (.a(negator_1_out), .b(negator_2_out), .out(TEMP));  // open: cin, cout
  Negator #(.width(32)) negator_2 (.in(multiplier_5_out), .out(negator_2_out));
  Adder #(.width(32)) adder_6 (.a(multiplier_4_cout), .b(multiplier_5_cout), .out(adder_6_out));  // open: cin, cout
  Negator #(.width(32)) negator_3 (.in(adder_6_out), .out(negator_3_out));
  Multiplexer #(.select(4), .width(32), .enable("false")) multiplexer_4 (
    .in0(ADD0), .in1(AND0), .in2(OR0), .in3(XOR0), .in4(SRL0), .in5(SRA0), .in6(SLL0), .in7(SLT0),
    .in8(DIVU0), .in9(REMU0), .in10(MUL0), .in11(MULHU0), .in12(SUB0), .in13(BSEL0), .in14(MULH0),
    .in15({32{1'b0}}), .out(Result), .sel(ALUSel));
  // Probe on MULH0
  Multiplexer #(.width(32), .enable("false")) multiplexer_5 (
    .in0(negator_3_out), .in1(subtractor_2_out), .out(multiplexer_5_out), .sel(negator_3_out[31]));
  Subtractor #(.width(32)) subtractor_2 (.a(negator_3_out), .b(32'h1), .out(subtractor_2_out));  // open: bin, bout

  // Other names for the same wires on the sheet: AVAL[30:0] = A[30:0]; BVAL[30:0] = B[30:0]

  // Notes on the sheet:
  //   INPUTS to your circuit
  //   DON'T CHANGE THE LOCATIONS OF THE INPUTS AND OUTPUTS!
  //   OUTPUT from your circuit
endmodule
