// Logisim project cpu.circ as structural Verilog: 1 circuit, main circuit main
module main (
  input  [31:0] INSTRUCTION,
  input  CLOCK,
  output [31:0] PROGRAM_COUNTER,
  output [31:0] ra,
  output [31:0] sp,
  output [31:0] t0,
  output [31:0] t1,
  output [31:0] t2,
  output [31:0] s0,
  output [31:0] s1,
  output [31:0] a0
);

  wire ASEL, BREQ, BRLT, BRlt_t, BRUN, BSEL, MEM, PCSEL, WRITE;
  wire [1:0] WBSEL;
  wire [2:0] IMMSEL;
  wire [3:0] ALUSEL;
  wire [31:0] ALUA, ALUB, DMEM_p5, IMMS, multiplexer_1_out, PC4, PCL, PIPINS, PIPPC, RS1, RS2, WBO;

  control_logic control_logic_1 (
    .BSel(BSEL), .ASel(ASEL), .BrUn(BRUN), .ImmSel(IMMSEL), .RegWEn(WRITE), .PCSel(PCSEL), .BrLt(BRLT),
    .BrEq(BREQ), .inst(PIPINS), .ALUSel(ALUSEL), .MemRW(MEM), .WBSel(WBSEL));
  Multiplexer #(.width(32), .enable("false")) multiplexer_1 (
    .in0(PC4), .in1(PCL), .out(multiplexer_1_out), .sel(PCSEL));
  // Probe on PCSEL
  Adder #(.width(32)) adder_1 (.a(PROGRAM_COUNTER), .b(32'h4), .out(PC4));  // open: cin, cout
  Register #(.width(32)) PC (.D(multiplexer_1_out), .clk(CLOCK), .Q(PROGRAM_COUNTER));  // open: en, clr
  imm_gen imm_gen_1 (.ImmSel(IMMSEL), .inst(PIPINS), .imm(IMMS));
  // Probe on IMMS
  Register #(.width(32)) register_1 (.D(PROGRAM_COUNTER), .clk(CLOCK), .Q(PIPPC));  // open: en, clr
  branch_comp branch_comp_1 (.BrEq(BREQ), .BrUn(BRUN), .rs1(RS1), .BrLt(BRlt_t), .rs2(RS2));
  // Probe on PIPPC
  Register #(.width(32)) register_2 (.D(INSTRUCTION), .clk(CLOCK), .Q(PIPINS));  // open: en, clr
  // Probe on PIPINS
  regfile_main RegFile (
    .rs2(PIPINS[24:20]), .rd(PIPINS[11:7]), .Read_Data_1(RS1), .Read_Data_2(RS2), .ra(ra), .sp(sp), .t0(t0),
    .t1(t1), .t2(t2), .s0(s0), .s1(s1), .a0(a0), .rs1(PIPINS[19:15]), .Write_Data(WBO), .RegWEn(WRITE),
    .clk(CLOCK));
  Multiplexer #(.width(32), .enable("false")) multiplexer_2 (.in0(RS1), .in1(PIPPC), .out(ALUA), .sel(ASEL));
  Multiplexer #(.width(32), .enable("false")) multiplexer_3 (.in0(RS2), .in1(IMMS), .out(ALUB), .sel(BSEL));
  // Probe on ALUA
  // Probe on ALUB
  alu Arithmetic_Logic_Unit (.ALUSel(ALUSEL), .Result(PCL), .B(ALUB), .A(ALUA));
  // Probe on ALUSEL
  // mem_main DMEM: pin names not known; wires that end beside it: PCL, RS2, CLOCK, MEM, DMEM_p5
  Multiplexer #(.select(2), .width(32), .enable("false")) multiplexer_4 (
    .in0(DMEM_p5), .in1(PCL), .in2(PC4), .out(WBO), .sel(WBSEL));  // open: in3

  // Other names for the same wires on the sheet: clk = CLOCK

  // Notes on the sheet:
  //   Output
  //   IMEM (do **NOT** move this)
  //   Inputs
  //   It is OK to move the PC, RegFile, ALU, MEM, Branch Comp, Imm Gen, and Control Logic to wherever is most convenient for you when constructing your CPU, and to delete this text
  //   Inputs/Outputs for testing. Do **NOT** move these.
endmodule
