// Logisim project control_logic.circ as structural Verilog: 1 circuit, main circuit control_logic
module control_logic (
  input  [31:0] inst,
  input  BrEq,
  input  BrLt,
  output PCSel,
  output RegWEn,
  output [2:0] ImmSel,
  output BrUn,
  output ASel,
  output BSel,
  output [3:0] ALUSel,
  output MemRW,
  output [1:0] WBSel
);

  wire ADD1, ADDI, AND1, and_3_out, and_4_out, and_5_out, and_6_out, and_7_out, and_41_out, and_42_out,
       and_43_out, and_44_out, and_45_out, and_46_out, and_54_out, ANDI, BEQ, BGE, BGEU, BLT, BLTU, BNE,
       comparator_1_eq, comparator_2_eq, comparator_12_eq, comparator_13_eq, comparator_14_eq,
       comparator_15_eq, comparator_16_eq, comparator_17_eq, comparator_18_eq, comparator_19_eq,
       comparator_20_eq, comparator_21_eq, comparator_22_eq, comparator_23_eq, comparator_24_eq,
       comparator_25_eq, comparator_26_eq, comparator_27_eq, comparator_28_eq, comparator_29_eq,
       comparator_30_eq, comparator_31_eq, comparator_32_eq, comparator_33_eq, comparator_34_eq,
       comparator_35_eq, comparator_36_eq, comparator_37_eq, comparator_38_eq, comparator_39_eq,
       comparator_40_eq, comparator_41_eq, comparator_42_eq, comparator_43_eq, comparator_44_eq,
       comparator_45_eq, comparator_46_eq, comparator_47_eq, comparator_48_eq, comparator_49_eq,
       comparator_50_eq, comparator_51_eq, DIVU, IL, IM, IM5, IMSel, JAL, JALR, LB, LH, LW, MLHU, MUL1, MULH,
       not_1_out, not_2_out, not_3_out, OR01, or_5_out, or_6_out, or_7_out, or_12_out, or_13_out, or_14_out,
       or_15_out, or_16_out, or_17_out, or_18_out, ORI, R, R30, R31, R32, R33, R34, R35, R36, R37, REMU, S,
       SB, SLL1, SLLI, SLT1, SLTI, SRA1, SRAI, SRL1, SRLI, SUB1, SW, SWLT, UIM, UMSel, UPC, XOR1, XORI;
  wire [1:0] multiplexer_6_out;
  wire [3:0] ALUBSel, ANDSel, DIVUSel, MLHUSel, MULHSel, MULSel, ORSel, REMUSel, SLLSel, SLTSel, SRASel,
       SRLSel, SUBSel, XORSel;

  Comparator #(.width(7)) comparator_1 (.a({7{1'b0}}), .b(inst[31:25]), .eq(comparator_1_eq));  // open: gt, lt
  Comparator #(.width(7)) comparator_2 (.a(7'b0100000), .b(inst[31:25]), .eq(comparator_2_eq));  // open: gt, lt
  // Probe on R
  Comparator #(.width(7)) comparator_3 (.a(inst[6:0]), .b(7'b0110011), .eq(R));  // open: gt, lt
  // Probe on IL
  Comparator #(.width(7)) comparator_4 (.a(inst[6:0]), .b(7'b0000011), .eq(IL));  // open: gt, lt
  // Probe on IM
  Comparator #(.width(7)) comparator_5 (.a(inst[6:0]), .b(7'b0010011), .eq(IM));  // open: gt, lt
  // Probe on S
  Comparator #(.width(7)) comparator_6 (.a(inst[6:0]), .b(7'b0100011), .eq(S));  // open: gt, lt
  // Probe on SB
  Comparator #(.width(7)) comparator_7 (.a(inst[6:0]), .b(7'b1100011), .eq(SB));  // open: gt, lt
  // Probe on UPC
  Comparator #(.width(7)) comparator_8 (.a(inst[6:0]), .b(7'b0010111), .eq(UPC));  // open: gt, lt
  // Probe on UIM
  Comparator #(.width(7)) comparator_9 (.a(inst[6:0]), .b(7'b0110111), .eq(UIM));  // open: gt, lt
  // Probe on JAL
  Comparator #(.width(7)) comparator_10 (.a(inst[6:0]), .b(7'b1101111), .eq(JAL));  // open: gt, lt
  // Probe on JALR
  Comparator #(.width(7)) comparator_11 (.a(inst[6:0]), .b(7'b1100111), .eq(JALR));  // open: gt, lt
  and and_1 (SRLI, IM5, comparator_1_eq);
  and and_2 (SRAI, IM5, comparator_2_eq);
  or or_1 (IMSel, IL, IM, JALR);
  or or_2 (UMSel, UPC, UIM);
  Priority_Encoder priority_encoder_1 (
    .in0(R), .in1(IMSel), .in2(S), .in3(SB), .in4(UMSel), .in5(JAL), .out(ImmSel));  // open: in6, in7, en_in, gs, en_out
  // Probe on ImmSel
  or or_3 (RegWEn, R, IL, IM, UPC, UIM, JAL, JALR);
  assign ALUSel = 4'b0000 | ANDSel | ORSel | XORSel | SRLSel | SRASel | SLLSel | SLTSel | DIVUSel | REMUSel | MULSel | MLHUSel | SUBSel | ALUBSel | MULHSel;  // OR_Gate or_4, 4 bits wide
  and and_3 (and_3_out, R, 1'b1);
  and and_4 (and_4_out, IL, 1'b1);
  and and_5 (and_5_out, IM, 1'b1);
  and and_6 (and_6_out, S, 1'b1);
  and and_7 (and_7_out, SB, 1'b1);
  Comparator #(.width(3)) comparator_12 (.a(3'b000), .b(inst[14:12]), .eq(comparator_12_eq));  // open: gt, lt
  Comparator #(.width(3)) comparator_13 (.a(3'b001), .b(inst[14:12]), .eq(comparator_13_eq));  // open: gt, lt
  Comparator #(.width(3)) comparator_14 (.a(3'b010), .b(inst[14:12]), .eq(comparator_14_eq));  // open: gt, lt
  Comparator #(.width(3)) comparator_15 (.a(3'b011), .b(inst[14:12]), .eq(comparator_15_eq));  // open: gt, lt
  Comparator #(.width(3)) comparator_16 (.a(3'b100), .b(inst[14:12]), .eq(comparator_16_eq));  // open: gt, lt
  Comparator #(.width(3)) comparator_17 (.a(3'b101), .b(inst[14:12]), .eq(comparator_17_eq));  // open: gt, lt
  Comparator #(.width(3)) comparator_18 (.a(3'b110), .b(inst[14:12]), .eq(comparator_18_eq));  // open: gt, lt
  Comparator #(.width(3)) comparator_19 (.a(3'b111), .b(inst[14:12]), .eq(comparator_19_eq));  // open: gt, lt
  Comparator #(.width(3)) comparator_20 (.a(3'b000), .b(inst[14:12]), .eq(comparator_20_eq));  // open: gt, lt
  Comparator #(.width(3)) comparator_21 (.a(3'b001), .b(inst[14:12]), .eq(comparator_21_eq));  // open: gt, lt
  Comparator #(.width(3)) comparator_22 (.a(3'b010), .b(inst[14:12]), .eq(comparator_22_eq));  // open: gt, lt
  Comparator #(.width(3)) comparator_23 (.a(3'b000), .b(inst[14:12]), .eq(comparator_23_eq));  // open: gt, lt
  Comparator #(.width(3)) comparator_24 (.a(3'b001), .b(inst[14:12]), .eq(comparator_24_eq));  // open: gt, lt
  Comparator #(.width(3)) comparator_25 (.a(3'b010), .b(inst[14:12]), .eq(comparator_25_eq));  // open: gt, lt
  Comparator #(.width(3)) comparator_26 (.a(3'b100), .b(inst[14:12]), .eq(comparator_26_eq));  // open: gt, lt
  Comparator #(.width(3)) comparator_27 (.a(3'b101), .b(inst[14:12]), .eq(comparator_27_eq));  // open: gt, lt
  Comparator #(.width(3)) comparator_28 (.a(3'b110), .b(inst[14:12]), .eq(comparator_28_eq));  // open: gt, lt
  Comparator #(.width(3)) comparator_29 (.a(3'b111), .b(inst[14:12]), .eq(comparator_29_eq));  // open: gt, lt
  Comparator #(.width(3)) comparator_30 (.a(3'b010), .b(inst[14:12]), .eq(comparator_30_eq));  // open: gt, lt
  Comparator #(.width(3)) comparator_31 (.a(3'b111), .b(inst[14:12]), .eq(comparator_31_eq));  // open: gt, lt
  Comparator #(.width(3)) comparator_32 (.a(3'b000), .b(inst[14:12]), .eq(comparator_32_eq));  // open: gt, lt
  Comparator #(.width(3)) comparator_33 (.a(3'b001), .b(inst[14:12]), .eq(comparator_33_eq));  // open: gt, lt
  Comparator #(.width(3)) comparator_34 (.a(3'b100), .b(inst[14:12]), .eq(comparator_34_eq));  // open: gt, lt
  Comparator #(.width(3)) comparator_35 (.a(3'b101), .b(inst[14:12]), .eq(comparator_35_eq));  // open: gt, lt
  Comparator #(.width(3)) comparator_36 (.a(3'b110), .b(inst[14:12]), .eq(comparator_36_eq));  // open: gt, lt
  Comparator #(.width(3)) comparator_37 (.a(3'b111), .b(inst[14:12]), .eq(comparator_37_eq));  // open: gt, lt
  and and_8 (R30, and_3_out, comparator_12_eq);
  and and_9 (R31, and_3_out, comparator_13_eq);
  and and_10 (R32, and_3_out, comparator_14_eq);
  and and_11 (R33, and_3_out, comparator_15_eq);
  and and_12 (R34, and_3_out, comparator_16_eq);
  and and_13 (R35, and_3_out, comparator_17_eq);
  and and_14 (R36, and_3_out, comparator_18_eq);
  and and_15 (R37, and_3_out, comparator_19_eq);
  and and_16 (LB, and_4_out, comparator_20_eq);
  and and_17 (LH, and_4_out, comparator_21_eq);
  and and_18 (LW, and_4_out, comparator_22_eq);
  and and_19 (ADDI, and_5_out, comparator_23_eq);
  and and_20 (SLLI, and_5_out, comparator_24_eq);
  and and_21 (SLTI, and_5_out, comparator_25_eq);
  and and_22 (XORI, and_5_out, comparator_26_eq);
  and and_23 (IM5, and_5_out, comparator_27_eq);
  and and_24 (ORI, and_5_out, comparator_28_eq);
  and and_25 (ANDI, and_5_out, comparator_29_eq);
  and and_26 (SW, and_6_out, comparator_30_eq);
  and and_27 (SWLT, and_6_out, comparator_31_eq);
  and and_28 (BEQ, and_7_out, comparator_32_eq);
  and and_29 (BNE, and_7_out, comparator_33_eq);
  and and_30 (BLT, and_7_out, comparator_34_eq);
  and and_31 (BGE, and_7_out, comparator_35_eq);
  and and_32 (BLTU, and_7_out, comparator_36_eq);
  and and_33 (BGEU, and_7_out, comparator_37_eq);
  Multiplexer #(.width(4), .enable("false")) multiplexer_1 (.in0(4'b0000), .in1(4'b0001), .out(ANDSel), .sel(or_5_out));
  or or_5 (or_5_out, ANDI, AND1);
  Multiplexer #(.width(4), .enable("false")) multiplexer_2 (.in0(4'b0000), .in1(4'b0010), .out(ORSel), .sel(or_6_out));
  or or_6 (or_6_out, ORI, OR01);
  Multiplexer #(.width(4), .enable("false")) multiplexer_3 (.in0(4'b0000), .in1(4'b0111), .out(SLTSel), .sel(or_7_out));
  or or_7 (or_7_out, SLTI, SLT1);
  Multiplexer #(.width(4), .enable("false")) multiplexer_4 (.in0(4'b0000), .in1(4'b1010), .out(MULSel), .sel(MUL1));
  Multiplexer #(.width(4), .enable("false")) multiplexer_5 (.in0(4'b0000), .in1(4'b1110), .out(MULHSel), .sel(MULH));
  Multiplexer #(.width(2), .enable("false")) multiplexer_6 (
    .in0(2'b01), .in1(2'b00), .out(multiplexer_6_out), .sel(IL));
  Comparator #(.width(7)) comparator_38 (.a({7{1'b0}}), .b(inst[31:25]), .eq(comparator_38_eq));  // open: gt, lt
  Comparator #(.width(7)) comparator_39 (.a(7'b0000001), .b(inst[31:25]), .eq(comparator_39_eq));  // open: gt, lt
  Comparator #(.width(7)) comparator_40 (.a(7'b0100000), .b(inst[31:25]), .eq(comparator_40_eq));  // open: gt, lt
  Comparator #(.width(7)) comparator_41 (.a({7{1'b0}}), .b(inst[31:25]), .eq(comparator_41_eq));  // open: gt, lt
  Comparator #(.width(7)) comparator_42 (.a(7'b0000001), .b(inst[31:25]), .eq(comparator_42_eq));  // open: gt, lt
  Comparator #(.width(7)) comparator_43 (.a({7{1'b0}}), .b(inst[31:25]), .eq(comparator_43_eq));  // open: gt, lt
  Comparator #(.width(7)) comparator_44 (.a(7'b0000001), .b(inst[31:25]), .eq(comparator_44_eq));  // open: gt, lt
  or or_8 (MemRW, 1'b0, S);
  or or_9 (BrUn, BLTU, BGEU);
  or or_10 (ASel, SB, JAL, UPC);
  or or_11 (BSel, IM, SB, JALR, JAL, UIM, UPC);
  Multiplexer #(.width(2), .enable("false")) multiplexer_7 (
    .in0(multiplexer_6_out), .in1(2'b10), .out(WBSel), .sel(or_12_out));
  or or_12 (or_12_out, JAL, JALR);
  // Probe on ADD1
  and and_34 (ADD1, R30, comparator_38_eq);
  // Probe on MUL1
  and and_35 (MUL1, R30, comparator_39_eq);
  // Probe on SUB1
  and and_36 (SUB1, R30, comparator_40_eq);
  // Probe on SLL1
  and and_37 (SLL1, R31, comparator_41_eq);
  // Probe on MULH
  and and_38 (MULH, R31, comparator_42_eq);
  // Probe on SLT1
  and and_39 (SLT1, R32, comparator_43_eq);
  // Probe on MLHU
  and and_40 (MLHU, R33, comparator_44_eq);
  or or_13 (or_13_out, XORI, XOR1);
  or or_14 (or_14_out, SRLI, SRL1);
  or or_15 (or_15_out, UIM, SB);
  Multiplexer #(.width(4), .enable("false")) multiplexer_8 (
    .in0(4'b0000), .in1(4'b0011), .out(XORSel), .sel(or_13_out));
  Multiplexer #(.width(4), .enable("false")) multiplexer_9 (
    .in0(4'b0000), .in1(4'b0100), .out(SRLSel), .sel(or_14_out));
  Multiplexer #(.width(4), .enable("false")) multiplexer_10 (
    .in0(4'b0000), .in1(4'b1101), .out(ALUBSel), .sel(or_15_out));
  Multiplexer #(.width(4), .enable("false")) multiplexer_11 (.in0(4'b0000), .in1(4'b1011), .out(MLHUSel), .sel(MLHU));
  Multiplexer #(.width(4), .enable("false")) multiplexer_12 (.in0(4'b0000), .in1(4'b1000), .out(DIVUSel), .sel(DIVU));
  not not_1 (not_1_out, BrEq);
  not not_2 (not_2_out, BrLt);
  not not_3 (not_3_out, BrLt);
  and and_41 (and_41_out, BrEq, BEQ);
  and and_42 (and_42_out, not_1_out, BNE);
  and and_43 (and_43_out, BLT, BrLt);
  and and_44 (and_44_out, BLTU, BrLt);
  and and_45 (and_45_out, BGE, not_2_out);
  and and_46 (and_46_out, BGEU, not_3_out);
  Comparator #(.width(7)) comparator_45 (.a({7{1'b0}}), .b(inst[31:25]), .eq(comparator_45_eq));  // open: gt, lt
  Comparator #(.width(7)) comparator_46 (.a(7'b0000001), .b(inst[31:25]), .eq(comparator_46_eq));  // open: gt, lt
  Comparator #(.width(7)) comparator_47 (.a(7'b0100000), .b(inst[31:25]), .eq(comparator_47_eq));  // open: gt, lt
  Comparator #(.width(7)) comparator_48 (.a({7{1'b0}}), .b(inst[31:25]), .eq(comparator_48_eq));  // open: gt, lt
  Comparator #(.width(7)) comparator_49 (.a(7'b0000001), .b(inst[31:25]), .eq(comparator_49_eq));  // open: gt, lt
  Comparator #(.width(7)) comparator_50 (.a({7{1'b0}}), .b(inst[31:25]), .eq(comparator_50_eq));  // open: gt, lt
  Comparator #(.width(7)) comparator_51 (.a({7{1'b0}}), .b(inst[31:25]), .eq(comparator_51_eq));  // open: gt, lt
  Multiplexer #(.width(4), .enable("false")) multiplexer_13 (
    .in0(4'b0000), .in1(4'b0101), .out(SRASel), .sel(or_16_out));
  or or_16 (or_16_out, SRAI, SRA1);
  Multiplexer #(.width(4), .enable("false")) multiplexer_14 (
    .in0(4'b0000), .in1(4'b0110), .out(SLLSel), .sel(or_17_out));
  or or_17 (or_17_out, SLLI, SLL1);
  Multiplexer #(.width(4), .enable("false")) multiplexer_15 (.in0(4'b0000), .in1(4'b1001), .out(REMUSel), .sel(REMU));
  Multiplexer #(.width(4), .enable("false")) multiplexer_16 (.in0(4'b0000), .in1(4'b1100), .out(SUBSel), .sel(SUB1));
  or or_18 (or_18_out, and_41_out, and_42_out, and_43_out, and_44_out, and_45_out, and_46_out);
  // Probe on SRL1
  and and_47 (SRL1, R35, comparator_45_eq);
  // Probe on DIVU
  and and_48 (DIVU, R35, comparator_46_eq);
  // Probe on SRA1
  and and_49 (SRA1, R35, comparator_47_eq);
  // Probe on AND1
  and and_50 (AND1, R37, comparator_48_eq);
  // Probe on REMU
  and and_51 (REMU, R37, comparator_49_eq);
  // Probe on OR01
  and and_52 (OR01, R36, comparator_50_eq);
  // Probe on XOR1
  and and_53 (XOR1, R34, comparator_51_eq);
  or or_19 (PCSel, JAL, JALR, and_54_out);
  and and_54 (and_54_out, or_18_out, SB);

  // Other names for the same wires on the sheet: OPcode[6:0] = inst[6:0]; RD[4:0] = inst[11:7];
  //   FUNC3[2:0] = inst[14:12]; RS1[4:0] = inst[19:15]; RS2[4:0] = inst[24:20]; FUNC7[6:0] = inst[31:25]

  // Notes on the sheet:
  //   INST Disassembler
  //   TYPE Disassembler
  //   IM-F7 Disassembler
  //   IMMSel
  //   ALUSel
  //   RegWEn
  //   INPUTS to your circuit
  //   R-F3 Disassembler
  //   IL-F3 Disassembler
  //   IM-F3 Disassembler
  //   S Disassembler
  //   SB-F3 Disassembler
  //   DON'T CHANGE THE LOCATIONS OF THE INPUTS AND OUTPUTS!
  //   OUTPUT from your circuit
  //   R-F7 Disassembler
  //   ALU Selector A
  //   MemRW
  //   BrUn
  //   ASel
  //   BSel
  //   WBSel
  //   PCSel
endmodule
