// Logisim project cpu.circ as structural Verilog: 1 circuit, main circuit main
module main (
  input  [31:0] INSTRUCTION,
  input  CLOCK,
  output [31:0] PROGRAM_COUNTER,
  output [31:0] ra,
  output [31:0] sp,
  output [31:0] t0,
  output [31:0] t1,
  output [31:0] t2,
  output [31:0] s0,
  output [31:0] s1,
  output [31:0] a0
);

  wire ASEL, BREQ, BRLT, BRUN, BSEL, comparator_1_eq, comparator_2_eq, JAL_R, MEM, PCSEL, PCSEL_S, PCSEL_X,
       PREV_VAL, WRITE;
  wire [1:0] WBSEL;
  wire [2:0] IMMSEL;
  wire [3:0] ALUSEL;
  wire [4:0] ADDR_A, ADDR_B, ADDR_D;
  wire [31:0] adder_2_out, ALU_M, ALUA, ALUB, DATA_A, DATA_B, DATA_R, IMMS_X, INST_D, multiplexer_7_out,
       multiplexer_8_out, PC_D, PC_M, PIPINS, subtractor_1_out, WD_D;

  control_logic control_logic_1 (
    .BSel(BSEL), .ASel(ASEL), .BrUn(BRUN), .ImmSel(IMMSEL), .RegWEn(WRITE), .PCSel(PCSEL), .BrLt(BRLT),
    .BrEq(BREQ), .inst(PIPINS), .ALUSel(ALUSEL), .MemRW(MEM), .WBSel(WBSEL));
  // Probe on PCSEL
  Multiplexer #(.width(32), .enable("false")) multiplexer_1 (
    .in0(PIPINS), .in1(32'h13), .out({INST_D[31:25], ADDR_B, ADDR_A, INST_D[14:12], ADDR_D, INST_D[6:0]}),
    .sel(PREV_VAL));
  Multiplexer #(.enable("false")) multiplexer_2 (.in0(PCSEL_S), .in1(1'b0), .out(PCSEL_X), .sel(PREV_VAL));
  Multiplexer #(.enable("false")) multiplexer_3 (.in0(PCSEL), .in1(1'b0), .out(PCSEL_S), .sel(PREV_VAL));
  branch_comp branch_comp_1 (.BrEq(BREQ), .BrUn(BRUN), .rs1(DATA_A), .BrLt(BRLT), .rs2(DATA_B));
  imm_gen imm_gen_1 (
    .ImmSel(IMMSEL), .imm(IMMS_X), .inst({INST_D[31:25], ADDR_B, ADDR_A, INST_D[14:12], ADDR_D, INST_D[6:0]}));
  // Probe on IMMS_X
  Register #(.width(32)) register_1 (.D(PROGRAM_COUNTER), .clk(CLOCK), .Q(PC_D));  // open: en, clr
  Register #(.width(32)) register_2 (.D(INSTRUCTION), .clk(CLOCK), .Q(PIPINS));  // open: en, clr
  Register #(.width(1)) register_3 (.D(PCSEL_X), .clk(CLOCK), .Q(PREV_VAL));  // open: en, clr
  Adder #(.width(32)) adder_1 (.a(PC_D), .b(32'h4), .out(PC_M));  // open: cin, cout
  Multiplexer #(.width(32), .enable("false")) multiplexer_4 (.in0(DATA_A), .in1(PC_D), .out(ALUA), .sel(ASEL));
  // Probe on ALUA
  Multiplexer #(.width(32), .enable("false")) multiplexer_5 (.in0(DATA_B), .in1(IMMS_X), .out(ALUB), .sel(BSEL));
  // Probe on ALUB
  Comparator #(.width(7)) comparator_1 (.a(7'b1101111), .b(INST_D[6:0]), .eq(comparator_1_eq));  // open: gt, lt
  or or_1 (JAL_R, comparator_1_eq, comparator_2_eq);
  Comparator #(.width(7)) comparator_2 (.a(INST_D[6:0]), .b(7'b1100111), .eq(comparator_2_eq));  // open: gt, lt
  Multiplexer #(.select(2), .width(32), .enable("false")) multiplexer_6 (
    .in0(DATA_R), .in1(ALU_M), .in2(PC_M), .out(WD_D), .sel(WBSEL));  // open: in3
  regfile_main RegFile (
    .rs2(ADDR_B), .rd(ADDR_D), .Read_Data_1(DATA_A), .Read_Data_2(DATA_B), .ra(ra), .sp(sp), .t0(t0),
    .t1(t1), .t2(t2), .s0(s0), .s1(s1), .a0(a0), .rs1(ADDR_A), .Write_Data(WD_D), .RegWEn(WRITE), .clk(CLOCK));
  Subtractor #(.width(32)) subtractor_1 (.a(ALU_M), .b(32'h4), .out(subtractor_1_out));  // open: bin, bout
  alu Arithmetic_Logic_Unit (.ALUSel(ALUSEL), .Result(ALU_M), .B(ALUB), .A(ALUA));
  Adder #(.width(32)) adder_2 (.a(PROGRAM_COUNTER), .b(multiplexer_7_out), .out(adder_2_out));  // open: cin, cout
  Multiplexer #(.width(32), .enable("false")) multiplexer_7 (
    .in0(32'h4), .in1(subtractor_1_out), .out(multiplexer_7_out), .sel(PCSEL_X));
  // mem_main DMEM: pin names not known; wires that end beside it: ALU_M, DATA_B, CLOCK, MEM, DATA_R
  Multiplexer #(.width(32), .enable("false")) multiplexer_8 (
    .in0(adder_2_out), .in1(ALU_M), .out(multiplexer_8_out), .sel(JAL_R));
  Register #(.width(32)) PC (.D(multiplexer_8_out), .clk(CLOCK), .Q(PROGRAM_COUNTER));  // open: en, clr
  // Probe on PIPINS
  // Probe on ALUA
  // Probe on PC_D
  // Probe on {INST_D[31:25], ADDR_B, ADDR_A, INST_D[14:12], ADDR_D, INST_D[6:0]}
  // Probe on ALUB
  // Probe on PC_D
  // Probe on DATA_A
  // Probe on ALU_M
  // Probe on IMMS_X
  // Probe on DATA_B
  // Probe on DATA_R
  // Probe on WD_D
  // Probe on PCSEL
  // Probe on BRUN
  // Probe on ASEL
  // Probe on WRITE
  // Probe on IMMSEL
  // Probe on ADDR_A
  // Probe on PCSEL_S
  // Probe on BRLT
  // Probe on BSEL
  // Probe on MEM
  // Probe on ALUSEL
  // Probe on ADDR_B
  // Probe on PREV_VAL
  // Probe on BREQ
  // Probe on JAL_R
  // Probe on INST_D[6:0]
  // Probe on ADDR_D

  // Other names for the same wires on the sheet: ALU_R[31:0] = ALU_M; clk = CLOCK;
  //   INST_M[31:0] = {INST_D[31:25], ADDR_B, ADDR_A, INST_D[14:12], ADDR_D, INST_D[6:0]};
  //   INST_W[31:0] = {INST_D[31:25], ADDR_B, ADDR_A, INST_D[14:12], ADDR_D, INST_D[6:0]};
  //   INST_X[31:0] = {INST_D[31:25], ADDR_B, ADDR_A, INST_D[14:12], ADDR_D, INST_D[6:0]}; OPCODE[6:0] = INST_D[6:0];
  //   INST_D (some bits) = {ADDR_B, ADDR_A, ADDR_D}; PC_X[31:0] = PC_D; RS1_X[31:0] = DATA_A; RS2_M[31:0] = DATA_B;
  //   RS2_X[31:0] = DATA_B; WD_W[31:0] = WD_D

  // Notes on the sheet:
  //   PIPELINE
  //   Output
  //   IMEM (do **NOT** move this)
  //   Inputs
  //   ALU INPUT SEL
  //   INST DECODER
  //   JUMPER DECODER
  //   WB SELECTOR
  //   PC COUNTER
  //   It is OK to move the PC, RegFile, ALU, MEM, Branch Comp, Imm Gen, and Control Logic to wherever is most convenient for you when constructing your CPU, and to delete this text
  //   Inputs/Outputs for testing. Do **NOT** move these.
  //   MONITOR
endmodule
