// Logisim project imm_gen.circ as structural Verilog: 1 circuit, main circuit imm_gen
module imm_gen (
  input  [31:0] inst,
  input  [2:0] ImmSel,
  output [31:0] imm
);

  wire [31:0] I2, S2, SB2, UJ2;

  assign I2 = {{20{inst[31]}}, inst[31:20]};  // Bit_Extender bit_extender_1
  // Probe on I2
  assign S2 = {{20{inst[31]}}, {inst[31:25], inst[11:7]}};  // Bit_Extender bit_extender_2
  // Probe on S2
  assign SB2 = {{19{inst[31]}}, {inst[31], inst[7], inst[30:25], inst[11:8], 1'b0}};  // Bit_Extender bit_extender_3
  // Probe on SB2
  // Probe on {inst[31:12], {12{1'b0}}}
  assign UJ2 = {{11{inst[31]}}, {inst[31], inst[19:12], inst[20], inst[30:21], 1'b0}};  // Bit_Extender bit_extender_4
  // Probe on UJ2
  Multiplexer #(.select(3), .width(32), .enable("false")) multiplexer_1 (
    .in1(I2), .in2(S2), .in3(SB2), .in4({inst[31:12], {12{1'b0}}}), .in5(UJ2), .out(imm), .sel(ImmSel));  // open: in0, in6, in7

  // Other names for the same wires on the sheet: SB1_4[3:0] = inst[11:8]; SIM1[4:0] = inst[11:7]; SB11 = inst[7];
  //   IIM1[11:0] = inst[31:20]; U2[31:12] = inst[31:12]; UIM[19:0] = inst[31:12]; UJ1_10[9:0] = inst[30:21];
  //   SB5_10[5:0] = inst[30:25]; SIM2[6:0] = inst[31:25]; UJ11 = inst[20]; UJ12_19[7:0] = inst[19:12];
  //   SB12 = inst[31]; UJ31 = inst[31]

  // Notes on the sheet:
  //   INPUTS to your circuit
  //   IMM Decoder
  //   IMM Assembler
  //   DON'T CHANGE THE LOCATIONS OF THE INPUTS AND OUTPUTS!
  //   OUTPUT from your circuit
endmodule
